# Fritzing sketch esquema (saved by Fritzing 0.9.4)
breadboards: 1

parts:
  MQ-135 = MQ-7 breakout
  YwRobot_Power_Supply2 = YwRobot Breadboard Power Supply [part_number=545043]
  U2 = ESP8266 WiFi Module [part_number=ESP8266]
  Componente2 = Arduino Uno (Rev3) - ICSP
  R = Resistor [tolerance=±5% resistance=220 package="2512 [SMD]"]
  LED = smd LED [color="Red (633nm)" package="0805 [SMD]"]
  LCD_20x4_I2C = LCD screen  # not connected
  LCM1602_IIC3 = LCM1602 IIC [part_number="LCM1602 IIC" chip_label="LCM1602 IIC" package="DIP (Dual Inline) [THT]"]
  DHT1 = DHT11 Humitidy and Temperature Sensor
  RTC = ZS-042 RTC Module
  Buzzer_activo = KY-012 Active Buzzer Module [package="Breakout board"]

nets:
  VCC: MQ-135.VCC, YwRobot_Power_Supply2.VCC#5, YwRobot_Power_Supply2.VCC#6, LCM1602_IIC3.VCC, DHT1.VDD, RTC.VCC
  GND: MQ-135.GND, YwRobot_Power_Supply2.GND, U2.GND, Componente2.GND, LED.cathode, LCM1602_IIC3.GND, DHT1.GND, RTC.GND, Buzzer_activo.-
  N1: MQ-135.DO, Componente2.D9_PWM
  N2: MQ-135.AO, Componente2.A0
  N3: YwRobot_Power_Supply2.VCC#9, YwRobot_Power_Supply2.VCC#10, U2.VCC, U2.RST, U2.CH_PD
  N4: U2.RXD, Componente2.D12/MISO
  N5: U2.TXD, Componente2.D11_PWM/MOSI
  N6: Componente2.A4/SDA, LCM1602_IIC3.SDA, RTC.SDA
  N7: Componente2.A5/SCL, LCM1602_IIC3.SCL, RTC.SCL
  N8: Componente2.D2, DHT1.DATA
  N9: Componente2.D4, R.Pin_1
  N10: Componente2.D6_PWM, Buzzer_activo.S
  N11: R.Pin_0, LED.anode

notes:
  3V
  5V

custom parts:
  MQ-7 breakout: SKU: 101282
  YwRobot Breadboard Power Supply: The YwRobot Breadboard Power Supply (MB-V2) has two power rails; they can be 5V or 3V3. Power to the module can be provided through the female USB socket or through the A10 (female) 2.1mm power jack.
  ESP8266 WiFi Module: Generic WiFi Module based on the ESP8266 with onboard PCB antenna and UART communications
  LCD screen: A standard character display, usually with 2x16 characters. Comes in many colors.
  LCM1602 IIC: I2C-Module to use a 1602 or 2004 LCD on with the wire.h libory Serial LCD Modul
  DHT11 Humitidy and Temperature Sensor: DHT11 Humidity and Temperature Sensor
  KY-012 Active Buzzer Module: Active Piezoelectric Buzzer Module Keyes KY-012, it produces single-tone sound when signal is high.
